// Logisim project bip.circ as structural Verilog: 1 circuit, main circuit main
module main (
  input  [3:0] in_1
);

  wire clock_1_out;
  wire [1:0] pla_1_out_2;
  wire [8:0] pla_1_out;
  wire [15:0] ACC_q, adder_1_out, adder_2_out, multiplexer_1_out, multiplexer_2_out, multiplexer_3_out,
       ram_1_dout, register_1_q, rom_1_data, subtractor_1_out;

  Register #(.width(16)) register_1 (.D(adder_1_out), .clk(clock_1_out), .Q(register_1_q));  // open: en, clr
  Adder #(.width(16)) adder_1 (.a(register_1_q), .b(16'h1), .out(adder_1_out));  // open: cin, cout
  Clock clock_1 (.out(clock_1_out));
  ROM #(.addrWidth(16), .dataWidth(16)) rom_1 (.addr(register_1_q), .data(rom_1_data));
  // Probe on rom_1_data
  PLA #(.in_width(4), .out_width(9), .\table ("0000 000000000 # NOP\n0001 111100000 # STO\n0010 011111000 # LD\n0011 001110100 # LDI\n0100 011110010 # ADD\n0101 001110000 # ADDI\n0110 011110011 # SUB\n0111 001110001 # SUBI")) pla_1 (
    .in(rom_1_data[15:12]), .out({pla_1_out[8:4], pla_1_out_2, pla_1_out[1:0]}));
  // Probe on rom_1_data[15:12]
  Multiplexer #(.width(16)) multiplexer_1 (
    .in0({in_1, rom_1_data[11:0]}), .in1(ram_1_dout), .out(multiplexer_1_out), .sel(pla_1_out[7]));
  // Probe on pla_1_out[0]
  // Probe on pla_1_out[1]
  // Probe on pla_1_out_2[0]
  // Probe on pla_1_out_2[1]
  // Probe on pla_1_out[4]
  // Probe on pla_1_out[5]
  // Probe on pla_1_out[6]
  // Probe on pla_1_out[7]
  // Probe on pla_1_out[8]
  // Probe on ACC_q
  // Probe on multiplexer_1_out
  Adder #(.width(16)) adder_2 (.a(ACC_q), .b(multiplexer_1_out), .out(adder_2_out));  // open: cin, cout
  Subtractor #(.width(16)) subtractor_1 (.a(ACC_q), .b(multiplexer_1_out), .out(subtractor_1_out));  // open: bin, bout
  // Probe on {in_1, rom_1_data[11:0]}
  // Probe on multiplexer_2_out
  Multiplexer #(.width(16)) multiplexer_2 (
    .in0(adder_2_out), .in1(subtractor_1_out), .out(multiplexer_2_out), .sel(pla_1_out[0]));
  // Probe on multiplexer_3_out
  Multiplexer #(.select(2), .width(16)) multiplexer_3 (
    .in0(multiplexer_2_out), .in1({in_1, rom_1_data[11:0]}), .in2(ram_1_dout), .out(multiplexer_3_out),
    .sel(pla_1_out_2));  // open: in3
  Register #(.width(16)) ACC (.D(multiplexer_3_out), .clk(clock_1_out), .Q(ACC_q));  // open: en, clr
  // Probe on ACC_q
  RAM #(.addrWidth(16), .dataWidth(16)) ram_1 (
    .addr({in_1, rom_1_data[11:0]}), .we(pla_1_out[8]), .clk(clock_1_out), .din(ACC_q), .dout(ram_1_dout));  // open: oe
  // Probe on ram_1_dout

  // Notes on the sheet:
  //   contents of rom_1 (hex, n*v repeats v):
  //   0 5015 5015 700a 5020 5020 5046
endmodule
